# Fritzing sketch Diagram_v1 (saved by Fritzing 0.9.3b)
breadboards: 1

parts:
  Part1 = Arduino Uno (Rev3)
  Part2 = Real Time Clock Module - DS1307 RTC Breakout Board
  Air_Pump_Relay = WeMos D1 Mini Relay Shield V2
  Filter_Relay = WeMos D1 Mini Relay Shield V2
  Feeder-1_Servo = Basic Servo
  Feeder-2_Servo = Basic Servo
  LED_Strip_WS2812B = WeMos D1 Mini WS2812B RGB Shield
  R1 = Resistor [tolerance=±5% resistance=220 package="2512 [SMD]"]
  C1_1000uF = Capacitor Polarized [package=panasonic_d]
  R2 = Resistor [tolerance=±5% resistance=10k package="0603 [SMD]"]
  S1 = Momentary Switch [package=ksa_sealed_tac_switch]
  Buzzer = Piezo Speaker
  Power_plug1 = Power plug

nets:
  N1: Part1.A4/SDA, Part2.SDA
  N2: Part1.A5/SCL, Part2.SCL
  N3: Part1.D8, S1.2
  N4: Part1.D9_PWM, Feeder-1_Servo.pulse, Feeder-2_Servo.pulse
  N5: Part1.D2, Filter_Relay.D4
  N6: Part1.D4, Air_Pump_Relay.D4
  N7: Part1.D6_PWM, R1.Pin_0
  N8: Part1.D7, Buzzer.pin2
  GND: Part1.GND, Part2.GND, Air_Pump_Relay.G, Filter_Relay.G, Feeder-2_Servo.gnd, LED_Strip_WS2812B.G, C1_1000uF.-, R2.Pin_1, Buzzer.pin1, Power_plug1.GND
  5V: Part1.VIN, Part2.5V, Air_Pump_Relay.5V, Filter_Relay.5V, Feeder-1_Servo.vcc, Feeder-2_Servo.vcc, LED_Strip_WS2812B.5V, C1_1000uF.+, S1.3, Power_plug1.VCC
  N9: LED_Strip_WS2812B.D4, R1.Pin_1
  N10: R2.Pin_0, S1.1
