# Fritzing sketch Diagram_v2 (saved by Fritzing 0.9.3b)
circuit board: 7.14034cm x 5.98729cm
breadboards: 1

parts:
  ARDUINO_NANO = Arduino Nano (Rev3.0)
  Power_plug1 = Power plug
  PAUSE = female pin header, 4 pins [form="♀ (female)"]
  NEOPIXEL = female pin header, 3 pins [form="♀ (female)"]
  RELAYS = female pin header, 6 pins [form="♀ (female)"]
  SERVOS = female pin header, 4 pins [form="♀ (female)"]
  RTC_DS1307 = female pin header, 5 pins [form="♀ (female)"]
  BUZZER = female pin header, 4 pins [form="♀ (female)"]

nets:
  GND: ARDUINO_NANO.GND, Power_plug1.GND, PAUSE.pin3, NEOPIXEL.pin2, RELAYS.pin5, SERVOS.pin3, RTC_DS1307.pin5, BUZZER.pin4
  N1: ARDUINO_NANO.D2, RELAYS.pin1
  N2: ARDUINO_NANO.D3, RELAYS.pin2
  N3: ARDUINO_NANO.D4, RELAYS.pin3
  N4: ARDUINO_NANO.D5, RELAYS.pin4
  N5: ARDUINO_NANO.D6, NEOPIXEL.pin1
  N6: ARDUINO_NANO.D7, BUZZER.pin1
  N7: ARDUINO_NANO.D10, SERVOS.pin2
  N8: ARDUINO_NANO.D11/MOSI, SERVOS.pin1
  N9: ARDUINO_NANO.D12/MISO, PAUSE.pin2
  VIN: ARDUINO_NANO.VIN, Power_plug1.VCC, PAUSE.pin4, NEOPIXEL.pin3, RELAYS.pin6, SERVOS.pin4, RTC_DS1307.pin4
  N10: ARDUINO_NANO.A5, RTC_DS1307.pin2
  N11: ARDUINO_NANO.A4, RTC_DS1307.pin3
  N12: ARDUINO_NANO.D13/SCK, PAUSE.pin1

notes:
  VCC
  VIN
  GND
  +
  -
  D
  5V
  BTN
  LED
  R2
  R1
  R4
  R3
  SDA
  DS
  SCL
  S2
  S1
