# Fritzing sketch Diagram_v3 (saved by Fritzing 0.9.3b)
perfboards: 1

parts:
  XTAL1 = Crystal [frequency="16 Mhz" package=SMD]
  C1 = Capacitor [package=cap-pth-small2]
  C2 = Capacitor [package=cap-pth-small2]
  J6 = Piezo Speaker
  J9 = Camdenboss CTB0158-2 [part_number=CTB0158-2 package=THT]  # not connected
  HLK-PM3 = HLK-PM01
  C4 = Electrolytic Capacitor [capacitance=10µF package="1010 [SMD, electrolytic]"]
  J12 = female pin header, 7 pins [form="♀ (female)"]
  J13 = female pin header, 7 pins [form="♀ (female)"]
  U2 = atmega328 [package=dip]
  J15 = female pin header, 7 pins [form="♀ (female)"]
  J10 = female pin header, 4 pins [form="♀ (female)"]
  R1 = Resistor [tolerance=±5% resistance=10k package=THT]

nets:
  N1: XTAL1.pin_0, C1.1, U2.XLAT1
  N2: XTAL1.pin_1, C2.2, U2.XLAT2
  N3: C1.2, C2.1
  N4: J6.pin2, U2.D2
  N5: HLK-PM3.-Vo, C4.+, J12.pin6, U2.GND, J15.pin2, J10.pin4
  N6: C4.-, J12.pin5, U2.VCC, U2.AVCC, J15.pin3, R1.Pin_1
  N7: J12.pin1, U2.D5_(PWM)
  N8: J12.pin2, U2.D6_(PWM)
  N9: J12.pin3, U2.D7
  N10: J12.pin4, U2.D8
  N11: J12.pin7, U2.D12
  N12: J13.pin7, U2.D13
  N13: U2.RESET, R1.Pin_0
  N14: U2.D9_(PWM), J10.pin1
  N15: U2.D10_(PWM), J10.pin2
  N16: U2.D11_(PWM), J10.pin3
